# Fritzing sketch Remote_Circuit_Diagram (saved by Fritzing 0.9.4)
breadboards: 1

parts:
  Arduino_Nano = Arduino Nano (Rev3.0)
  Joystick_X = Thumb Joystick
  Joystick_Y = Thumb Joystick
  NRF24L01_+_PA = NRF24L01+ Breakout Board
  BATT1 = LiPoly Battery (1300mAh)
  C1 = Electrolytic Capacitor [capacitance=1µF package="100 mil [THT, electrolytic]"]

nets:
  GND: Arduino_Nano.GND, Joystick_X.GND, Joystick_Y.GND, NRF24L01_+_PA.GND, C1.-
  N1: Arduino_Nano.D9, NRF24L01_+_PA.CE
  N2: Arduino_Nano.D10, NRF24L01_+_PA.CS
  N3: Arduino_Nano.D11/MOSI, NRF24L01_+_PA.MOSI
  N4: Arduino_Nano.D12/MISO, NRF24L01_+_PA.MISO
  VCC: Arduino_Nano.5V, Joystick_X.VCC, Joystick_Y.VCC
  N5: Arduino_Nano.A1, Joystick_Y.HORZ
  N6: Arduino_Nano.A0, Joystick_X.VERT
  3V3: Arduino_Nano.3V3, NRF24L01_+_PA.VCC, C1.+
  N7: Arduino_Nano.D13/SCK, NRF24L01_+_PA.SCK
  N8: BATT1.positive, BATT1.negative

custom parts:
  LiPoly Battery (1300mAh): Lithium Ion Polymer Battery (1300mAh)
