# Fritzing sketch Tank_Circuit_Diagram (saved by Fritzing 0.9.4)

parts:
  Parça1 = Arduino Uno (Rev3)
  L298N1 = L298N DC motor driver
  Parça2 = NRF24L01+ Breakout Board
  M1 = DC Motor  # not connected
  M2 = DC Motor  # not connected
  C1 = Electrolytic Capacitor [capacitance=1µF package="100 mil [THT, electrolytic]"]
  VCC1 = Battery  # not connected

nets:
  N1: Parça1.D8, L298N1.IN4
  N2: Parça1.D9_PWM, Parça2.CE
  N3: Parça1.D10_PWM/SS, Parça2.CS
  N4: Parça1.D11_PWM/MOSI, Parça2.MOSI
  N5: Parça1.D12/MISO, Parça2.MISO
  N6: Parça1.D13/SCK, Parça2.SCK
  N7: Parça1.D3_PWM, L298N1.ENA
  N8: Parça1.D4, L298N1.IN1
  N9: Parça1.D5_PWM, L298N1.IN2
  N10: Parça1.D6_PWM, L298N1.ENB
  N11: Parça1.D7, L298N1.IN3
  3V3: Parça1.3V3, Parça2.VCC, C1.+
  GND: Parça1.GND, Parça2.GND, C1.-

custom parts:
  L298N DC motor driver: 2x DC motor driver with 78M05 positive voltage regulator (7..35 V) L298N: max 46 V, 2 A Set 5 V Enable jumper to enable 5 V regultor (needed for the L298N) and +5 V output at screw terminal or supply external +5 V at screw terminal Set ENA and/or ENB to +5 V to enable motor permanently or supply ENA and/or ENB with PWM signal IN1 and IN2 set rotation directory for motor A (OUT1/OUT2) IN2 and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
